// Logisim project esercizio1.circ as structural Verilog: 3 circuits, main circuit punto1
module punto1 (
  input  A,
  input  B,
  input  C,
  input  D,
  output y1
);

  wire and_1_out, and_2_out, and_3_out, and_4_out, and_5_out;

  and and_1 (and_1_out, ~A, ~C, D);  // AND_Gate
  and and_2 (and_2_out, B, C, D);
  and and_3 (and_3_out, A, C, D);
  and and_4 (and_4_out, A, B);
  and and_5 (and_5_out, ~B, D);  // AND_Gate
  or or_1 (y1, and_1_out, and_2_out, and_3_out, and_4_out, and_5_out);
endmodule

module punto2 (
  input  A,
  input  B,
  input  D,
  output y2
);

  wire and_1_out;

  and and_1 (and_1_out, A, B);
  or or_1 (y2, and_1_out, D);
endmodule

module punto3 (
  input  A,
  input  B,
  input  C,
  input  D,
  output Y3
);

  wire punto1_1_y1, punto2_1_y2;

  punto1 punto1_1 (.y1(punto1_1_y1), .A(A), .B(B), .C(C), .D(D));
  punto2 punto2_1 (.A(A), .B(B), .D(D), .y2(punto2_1_y2));
  xnor xnor_1 (Y3, punto1_1_y1, punto2_1_y2);
endmodule
