// Logisim project esercizio2.circ as structural Verilog: 6 circuits, main circuit punto1
module punto1 (
  input  A,
  input  B,
  input  C,
  output y1
);

  wire and_1_out, and_2_out, and_3_out, and_4_out;

  and and_1 (and_1_out, ~A, ~B, ~C);  // AND_Gate
  and and_2 (and_2_out, ~A, B, C);  // AND_Gate
  and and_3 (and_3_out, A, ~B, ~C);  // AND_Gate
  and and_4 (and_4_out, A, ~B, C);  // AND_Gate
  or or_1 (y1, and_1_out, and_2_out, and_3_out, and_4_out);
endmodule

module punto2 (
  input  a,
  input  b,
  input  c,
  output y2
);

  wire and_1_a_and_b, and_2_a_and_b, and_4_a_and_b, and_6_a_and_b, m1, m2, m3, m4, not_1_not_a, not_2_not_a,
       not_3_not_a, not_4_not_a, not_5_not_a, not_6_not_a, not_7_not_a, or_1_a_or_b, or_2_a_or_b;

  \not  not_1 (.a(a), .not_a(not_1_not_a));
  \not  not_2 (.a(b), .not_a(not_2_not_a));
  \not  not_3 (.a(c), .not_a(not_3_not_a));
  \not  not_4 (.a(a), .not_a(not_4_not_a));
  \and  and_1 (.a(b), .b(c), .a_and_b(and_1_a_and_b));
  \not  not_5 (.a(b), .not_a(not_5_not_a));
  \not  not_6 (.a(c), .not_a(not_6_not_a));
  \not  not_7 (.a(b), .not_a(not_7_not_a));
  \and  and_2 (.a(not_1_not_a), .b(not_2_not_a), .a_and_b(and_2_a_and_b));
  \and  and_3 (.a(not_4_not_a), .b(and_1_a_and_b), .a_and_b(m2));
  \and  and_4 (.a(a), .b(not_5_not_a), .a_and_b(and_4_a_and_b));
  \and  and_5 (.a(and_4_a_and_b), .b(not_6_not_a), .a_and_b(m3));
  \and  and_6 (.a(a), .b(not_7_not_a), .a_and_b(and_6_a_and_b));
  \and  and_7 (.a(and_2_a_and_b), .b(not_3_not_a), .a_and_b(m1));
  \and  and_8 (.a(and_6_a_and_b), .b(c), .a_and_b(m4));
  \or  or_1 (.a(m1), .b(m2), .a_or_b(or_1_a_or_b));
  \or  or_2 (.a(or_1_a_or_b), .b(m3), .a_or_b(or_2_a_or_b));
  \or  or_3 (.a(or_2_a_or_b), .b(m4), .a_or_b(y2));
endmodule

module \not  (
  input  a,
  output not_a
);

  nand nand_1 (not_a, a, a);
endmodule

module \and  (
  input  a,
  input  b,
  output a_and_b
);

  wire nand_1_out;

  nand nand_1 (nand_1_out, a, b);
  \not  not_1 (.a(nand_1_out), .not_a(a_and_b));
endmodule

module \or  (
  input  a,
  input  b,
  output a_or_b
);

  wire not_1_not_a, not_2_not_a;

  \not  not_1 (.a(a), .not_a(not_1_not_a));
  \not  not_2 (.a(b), .not_a(not_2_not_a));
  nand nand_1 (a_or_b, not_1_not_a, not_2_not_a);
endmodule

// a
module punto3 (
  input  A,
  input  B,
  input  C,
  output Y3
);

  wire punto1_1_y1, punto2_1_y2;

  punto1 punto1_1 (.y1(punto1_1_y1), .A(A), .B(B), .C(C));
  punto2 punto2_1 (.a(A), .b(B), .c(C), .y2(punto2_1_y2));
  xnor xnor_1 (Y3, punto1_1_y1, punto2_1_y2);
endmodule
