// Logisim project esercizio3.circ as structural Verilog: 3 circuits, main circuit main
module main (
  input  in_1,
  output out_2
);

  wire clock_1_out, d_ff_1_q, d_ff_2_q, d_ff_3_q, next_1_b0_next, next_1_b1_next, next_1_b2_next;

  Clock clock_1 (.out(clock_1_out));
  D_Flip_Flop d_ff_1 (.clk(clock_1_out), .D(next_1_b0_next), .Q(d_ff_1_q));  // open: Qn, preset, en, reset
  D_Flip_Flop d_ff_2 (.clk(clock_1_out), .D(next_1_b1_next), .Q(d_ff_2_q));  // open: Qn, preset, en, reset
  D_Flip_Flop d_ff_3 (.clk(clock_1_out), .D(next_1_b2_next), .Q(d_ff_3_q));  // open: Qn, preset, en, reset
  next next_1 (
    .b0(d_ff_1_q), .b1(d_ff_2_q), .i(in_1), .b1_next(next_1_b1_next), .b2_next(next_1_b2_next),
    .b0_next(next_1_b0_next));
  out out_1 (.b0(d_ff_1_q), .b1(d_ff_2_q), .b2(d_ff_3_q), .y(out_2));

  // Other names for the same wires on the sheet: input = in_1
endmodule

module next (
  input  b0,
  input  b1,
  input  i,
  output b1_next,
  output b2_next,
  output b0_next
);


  assign b0_next = i;
  assign b1_next = b0;
  assign b2_next = b1;
endmodule

module out (
  input  b0,
  input  b1,
  input  b2,
  output y
);

  wire and_1_out, and_2_out, or_1_out;

  and and_1 (and_1_out, b1, b2);
  and and_2 (and_2_out, ~b1, ~b2);  // AND_Gate
  or or_1 (or_1_out, and_1_out, and_2_out);
  and and_3 (y, b0, or_1_out);
endmodule
