// Logisim project esercizio4.circ as structural Verilog: 1 circuit, main circuit main
module main (
  input  x1,
  input  x2,
  input  x3,
  input  x4,
  input  x5,
  output y
);

  wire and_2_out, and_3_out, and_4_out, and_5_out, and_6_out, d2, d3, d4, or_1_out, or_4_out;

  and and_1 (d2, x1, x2);
  and and_2 (and_2_out, x3, or_1_out);
  or or_1 (or_1_out, x1, x2);
  and and_3 (and_3_out, x3, d2);
  and and_4 (and_4_out, x4, d3);
  and and_5 (and_5_out, x5, d4);
  or or_2 (d3, d2, and_2_out);
  or or_3 (y, and_3_out, and_4_out, and_5_out);
  or or_4 (or_4_out, x1, x2, x3);
  and and_6 (and_6_out, x4, or_4_out);
  or or_5 (d4, d3, and_6_out);
endmodule
