// Logisim project esercizio1.circ as structural Verilog: 1 circuit, main circuit main
module main (
  input  b,
  input  c,
  input  a,
  input  d,
  output E
);

  wire and_1_out, xor_1_out;

  and and_1 (and_1_out, b, c);
  xor xor_1 (xor_1_out, and_1_out, a);
  or or_1 (E, xor_1_out, d);
endmodule
