// Logisim project esercizio2.circ as structural Verilog: 1 circuit, main circuit main
module main (
  input  [2:0] abc,
  input  [1:0] s,
  output out_3
);

  wire and_1_out, or_1_out;

  or or_1 (or_1_out, abc[2], and_1_out);
  and and_1 (and_1_out, abc[1], abc[0]);
  Multiplexer #(.select(2), .enable("false")) multiplexer_1 (
    .in0(abc[0]), .in1(abc[1]), .in2(abc[2]), .in3(or_1_out), .out(out_3), .sel(s));
endmodule
