// Logisim project esercizio3-4.circ as structural Verilog: 3 circuits, main circuit main
module fsm1 (
  input  Ck,
  input  rst,
  input  b_t,
  output W
);

  wire [1:0] next_1_s0_prime, register_1_q;

  Register #(.width(2)) register_1 (.D(next_1_s0_prime), .Q(register_1_q), .clk(Ck), .clr(rst));  // open: en
  next next_1 (
    .s0(register_1_q[0]), .s1(register_1_q[1]), .b_t(b_t), .s0_prime(next_1_s0_prime[0]),
    .s1_prime(next_1_s0_prime[1]));
  and and_1 (W, register_1_q[0], register_1_q[1]);

  // Other names for the same wires on the sheet: r = rst
endmodule

module next (
  input  s0,
  input  s1,
  input  b_t,
  output s0_prime,
  output s1_prime
);

  wire and_1_out, and_2_out, and_3_out;

  and and_1 (and_1_out, s0, s1);
  or or_1 (s0_prime, and_1_out, ~b_t);  // OR_Gate
  and and_2 (and_2_out, s0, b_t);
  or or_2 (s1_prime, and_2_out, and_3_out);
  and and_3 (and_3_out, s1, ~b_t);  // AND_Gate
endmodule

module main (
  input  b_t,
  input  c_t
);

  wire and_1_out, ck, counter_1_carry, fsm1_1_w, not_1_out, r;

  Button u_r (.out(r));
  Clock clock_1 (.out(ck));
  fsm1 fsm1_1 (.Ck(ck), .rst(r), .b_t(b_t), .W(fsm1_1_w));
  and and_1 (and_1_out, fsm1_1_w, not_1_out);
  not not_1 (not_1_out, c_t);
  LED led_1 (.in(fsm1_1_w));
  LED led_2 (.in(counter_1_carry));
  Counter #(.width(4), .max('hf), .ongoal("stay")) counter_1 (
    .count(and_1_out), .carry(counter_1_carry), .clk(ck), .clr(r));  // open: load, D, Q

  // Other names for the same wires on the sheet: b = b_t; c = c_t
endmodule
