// Logisim project ricopia.circ as structural Verilog: 1 circuit, main circuit main
module main (
  input  A,
  input  C,
  input  B,
  output nA,
  output nA_v_C,
  output nA_v_C_____A_v_B,
  output A_v_B
);

  not not_1 (nA, A);
  or or_1 (nA_v_C, nA, C);
  or or_2 (A_v_B, A, B);
  and and_1 (nA_v_C_____A_v_B, nA_v_C, A_v_B);
endmodule
