// Logisim project xnor.circ as structural Verilog: 1 circuit, main circuit main
module main (
  input  A,
  input  B,
  output A_XNOR_B
);

  wire and_1_out, not_1_out, or_1_out;

  or or_1 (or_1_out, A, B);
  and and_1 (and_1_out, B, A);
  not not_1 (not_1_out, or_1_out);
  or or_2 (A_XNOR_B, not_1_out, and_1_out);
endmodule
