// Logisim project equivalenza.circ as structural Verilog: 1 circuit, main circuit main
module main (
  input  A,
  input  B,
  input  C,
  output E1,
  output out_5,
  output E2
);

  wire and_1_out, and_2_out, and_3_out, and_4_out, not_1_out, not_2_out, not_3_out, not_4_out, or_1_out;

  not not_1 (not_1_out, A);
  not not_2 (not_2_out, C);
  not not_3 (not_3_out, B);
  and and_1 (and_1_out, not_1_out, B, not_2_out);
  and and_2 (and_2_out, A, B, not_2_out);
  and and_3 (and_3_out, A, not_3_out);
  and and_4 (and_4_out, A, C);
  or or_1 (or_1_out, and_1_out, and_2_out);
  or or_2 (E2, and_3_out, and_4_out);
  not not_4 (not_4_out, or_1_out);
  and and_5 (E1, not_4_out, A);
  xnor xnor_1 (out_5, E1, E2);
endmodule
