// Logisim project equivalenza2.circ as structural Verilog: 1 circuit, main circuit main
module main (
  input  A,
  input  B,
  input  C,
  output nA,
  output A_v_B,
  output A_NOR_B,
  output nB,
  output A_NOR_B_____C_v_nB,
  output C_v_nB,
  output nC
);

  wire nand_7_out;

  nand nand_1 (nA, A, A);
  nand nand_2 (nB, B, B);
  nand nand_3 (nC, C, C);
  nand nand_4 (A_v_B, nA, nB);
  nand nand_5 (C_v_nB, B, nC);
  nand nand_6 (A_NOR_B, A_v_B, A_v_B);
  nand nand_7 (nand_7_out, A_NOR_B, C_v_nB);
  nand nand_8 (A_NOR_B_____C_v_nB, nand_7_out, nand_7_out);
endmodule
