// Logisim project complemento_uno.circ as structural Verilog: 1 circuit, main circuit main
module main (
  input  [3:0] A,
  output [3:0] X
);

  not not_1 (X[0], A[0]);
  not not_2 (X[1], A[1]);
  not not_3 (X[2], A[2]);
  not not_4 (X[3], A[3]);
endmodule
