// Logisim project sop_xnor_1.circ as structural Verilog: 1 circuit, main circuit main
module main (
  input  A,
  input  B,
  output A_XNOR_B
);

  wire and_1_out, and_2_out;

  and and_1 (and_1_out, ~A, ~B);  // AND_Gate
  and and_2 (and_2_out, B, A);
  or or_1 (A_XNOR_B, and_1_out, and_2_out);
endmodule
