// Logisim project sop_xnor_2.circ as structural Verilog: 1 circuit, main circuit main
module main (
  input  A,
  input  B,
  output A_XNOR_B,
  output out_4,
  output A_XNOR_B_2
);

  wire and_1_out, and_2_out, and_3_out, not_1_out, or_1_out;

  or or_1 (or_1_out, A, B);
  not not_1 (not_1_out, or_1_out);
  and and_1 (and_1_out, B, A);
  and and_2 (and_2_out, ~A, ~B);  // AND_Gate
  and and_3 (and_3_out, B, A);
  or or_2 (A_XNOR_B, and_2_out, and_3_out);
  or or_3 (A_XNOR_B_2, not_1_out, and_1_out);
  xnor xnor_1 (out_4, A_XNOR_B, A_XNOR_B_2);
endmodule
