// Logisim project espressione_sop_semplificata.circ as structural Verilog: 1 circuit, main circuit main
module main (
  input  A,
  input  B,
  input  C,
  input  D,
  output out_5
);

  wire and_1_out, and_2_out, or_1_out, or_2_out;

  or or_1 (or_1_out, A, ~B);  // OR_Gate
  or or_2 (or_2_out, B, C);
  and and_1 (and_1_out, or_1_out, D);
  and and_2 (and_2_out, A, or_2_out);
  or or_3 (out_5, and_1_out, and_2_out);
endmodule
