// Logisim project circuit.circ as structural Verilog: 1 circuit, main circuit main
module main (
  input  A,
  input  B,
  input  C,
  output Y
);

  wire and_1_out, and_2_out, and_3_out;

  and and_1 (and_1_out, ~A, B);  // AND_Gate
  and and_2 (and_2_out, A, C);
  and and_3 (and_3_out, B, C);
  or or_1 (Y, and_1_out, ~and_2_out, and_3_out);  // OR_Gate
endmodule
