// Logisim project circuit.circ as structural Verilog: 1 circuit, main circuit main
module main (
  input  A,
  input  B,
  input  C,
  output out_4
);

  wire and_1_out, and_2_out, or_1_out, or_2_out;

  and and_1 (and_1_out, A, B);
  or or_1 (or_1_out, B, C);
  and and_2 (and_2_out, A, C);
  or or_2 (or_2_out, ~or_1_out, and_2_out);  // OR_Gate
  or or_3 (out_4, and_1_out, or_2_out);
endmodule
