// Logisim project fullader_HA.circ as structural Verilog: 2 circuits, main circuit HA
module HA (
  input  A,
  input  B,
  output R,
  output S
);

  xor xor_1 (S, A, B);
  and and_1 (R, A, B);
endmodule

module FA (
  input  A,
  input  B,
  input  Rin,
  output Rout,
  output S
);

  wire ha_1_r, ha_1_s, ha_2_r;

  HA ha_1 (.R(ha_1_r), .A(A), .B(B), .S(ha_1_s));
  HA ha_2 (.R(ha_2_r), .A(ha_1_s), .B(Rin), .S(S));
  or or_1 (Rout, ha_1_r, ha_2_r);
endmodule
