// Logisim project addizionatore4bit.circ as structural Verilog: 2 circuits, main circuit main
module main (
  input  [3:0] a,
  input  [3:0] b,
  output [4:0] a___b
);

  wire adder_1_cout, adder_2_cout, ha_1_r;

  HA ha_1 (.R(ha_1_r), .A(b[0]), .B(a[0]), .S(a___b[0]));
  Adder #(.width(1)) adder_1 (.a(a[1]), .b(b[1]), .out(a___b[1]), .cin(ha_1_r), .cout(adder_1_cout));
  Adder #(.width(1)) adder_2 (.a(a[2]), .b(b[2]), .out(a___b[2]), .cin(adder_1_cout), .cout(adder_2_cout));
  Adder #(.width(1)) adder_3 (.a(a[3]), .b(b[3]), .out(a___b[3]), .cin(adder_2_cout), .cout(a___b[4]));
endmodule

module HA (
  input  A,
  input  B,
  output R,
  output S
);

  xor xor_1 (S, A, B);
  and and_1 (R, A, B);
endmodule
