// Logisim project moltiplicatore3bit.circ as structural Verilog: 1 circuit, main circuit main
module main (
  input  [2:0] a,
  input  [2:0] b,
  output [5:0] out_3
);

  wire a0b1_out, a0b2_out, a1b0_out, a1b1_out, a1b2_out, a2b0_out, a2b1_out, a2b2_out, adder_1_cout,
       adder_2_out, adder_3_cout, adder_3_out, adder_4_cout, adder_5_cout;

  and a2b2 (a2b2_out, a[2], b[2]);
  and a1b2 (a1b2_out, a[1], b[2]);
  and a2b1 (a2b1_out, a[2], b[1]);
  and a0b2 (a0b2_out, a[0], b[2]);
  and a2b0 (a2b0_out, a[2], b[0]);
  and a1b1 (a1b1_out, a[1], b[1]);
  and a0b1 (a0b1_out, a[0], b[1]);
  and a0b0 (out_3[0], a[0], b[0]);
  and a1b0 (a1b0_out, a[1], b[0]);
  Adder #(.width(1)) adder_1 (.a(a1b0_out), .b(a0b1_out), .out(out_3[1]), .cout(adder_1_cout));  // open: cin
  Adder #(.width(1)) adder_2 (.a(a2b0_out), .b(a1b1_out), .out(adder_2_out), .cin(adder_1_cout));  // open: cout
  Adder #(.width(1)) adder_3 (.a(a2b1_out), .b(a1b2_out), .out(adder_3_out), .cout(adder_3_cout));  // open: cin
  Adder #(.width(1)) adder_4 (.a(adder_2_out), .b(a0b2_out), .out(out_3[2]), .cout(adder_4_cout));  // open: cin
  Adder #(.width(1)) adder_5 (.a(adder_4_cout), .b(adder_3_out), .out(out_3[3]), .cout(adder_5_cout));  // open: cin
  Adder #(.width(1)) adder_6 (.a(adder_3_cout), .b(a2b2_out), .out(out_3[4]), .cin(adder_5_cout), .cout(out_3[5]));

  // Notes on the sheet:
  //   S0
  //   S1
  //   S2
  //   S3
  //   S4
  //   S5
endmodule
