// Logisim project miniALU.circ as structural Verilog: 1 circuit, main circuit main
module main (
  input  [3:0] A,
  input  X,
  input  in_3,
  input  [3:0] B,
  output [3:0] out_5,
  output overflow,
  output [3:0] additional
);

  wire main_1_p5, or_1_out;
  wire [3:0] main_1_p4, n4_bit_multiplier_1_s0;

  // sommaDifferenzaOverflow_main main_1: pin names not known; wires that end beside it: B, B, in_3, main_1_p4, main_1_p5
  _4_bit_Multiplier u_4_bit_multiplier_1 (
    .A0(A[0]), .A1(A[1]), .A2(A[2]), .A3(A[3]), .B0(B[0]), .B1(B[1]), .B2(B[2]), .B3(B[3]),
    .S0(n4_bit_multiplier_1_s0[0]), .S1(n4_bit_multiplier_1_s0[1]), .S2(n4_bit_multiplier_1_s0[2]),
    .S3(n4_bit_multiplier_1_s0[3]), .S4(additional[0]), .S5(additional[1]), .S6(additional[2]),
    .S7(additional[3]));
  Multiplexer #(.width(4), .enable("false")) multiplexer_1 (
    .in0(main_1_p4), .in1(n4_bit_multiplier_1_s0), .out(out_5), .sel(X));
  Multiplexer #(.enable("false")) multiplexer_2 (.in0(main_1_p5), .in1(or_1_out), .out(overflow), .sel(X));
  or or_1 (or_1_out, additional[0], additional[1], additional[2], additional[3]);
endmodule
