// Logisim project sommaDifferenzaOverflow.circ as structural Verilog: 1 circuit, main circuit main
module main (
  input  [3:0] B,
  input  [3:0] A,
  input  in_3,
  output overflow,
  output [3:0] risultato
);

  wire xor_5_out, xor_6_out;
  wire [3:0] adder_1_out, bit_extender_1_out, xor_1_out;

  xor xor_1 (xor_1_out[0], in_3, B[0]);
  xor xor_2 (xor_1_out[1], in_3, B[1]);
  xor xor_3 (xor_1_out[2], in_3, B[2]);
  xor xor_4 (xor_1_out[3], in_3, B[3]);
  assign bit_extender_1_out = {{3{1'b0}}, in_3};  // Bit_Extender bit_extender_1
  Adder #(.width(4)) adder_1 (.a(bit_extender_1_out), .b(xor_1_out), .out(adder_1_out));  // open: cin, cout
  Adder #(.width(4)) adder_2 (.a(A), .b(adder_1_out), .out(risultato));  // open: cin, cout
  xor xor_5 (xor_5_out, A[3], risultato[3]);
  xor xor_6 (xor_6_out, risultato[3], adder_1_out[3]);
  and and_1 (overflow, xor_5_out, xor_6_out);

  // Notes on the sheet:
  //   A e B sono numeri in complemento a 2
  //   segno primo operando
  //   segno secondo operando
  //   segno risultato
endmodule
