// Logisim project bistabile_SOP_oscillazione.circ as structural Verilog: 1 circuit, main circuit Latch SC
module Latch_SC (
  input  Clear,
  input  Set,
  output out_3
);

  wire and_1_out, and_2_out, and_3_out;

  and and_1 (and_1_out, ~Clear, ~Set);  // AND_Gate
  and and_2 (and_2_out, ~Clear, Set);  // AND_Gate
  and and_3 (and_3_out, out_3, and_1_out);
  or or_1 (out_3, and_3_out, and_2_out);
endmodule
