// Logisim project bistabile_SOP_oscillazione_risolta.circ as structural Verilog: 1 circuit, main circuit Latch SR
module Latch_SR (
  input  Reset,
  input  in_2,
  input  Set,
  output out_4
);

  wire and_1_out, and_2_out, and_3_out, and_4_out;

  and and_1 (and_1_out, ~Reset, ~Set);  // AND_Gate
  and and_2 (and_2_out, ~Reset, Set);  // AND_Gate
  and and_3 (and_3_out, out_4, and_1_out);
  and and_4 (and_4_out, in_2, and_2_out);
  or or_1 (out_4, and_3_out, and_4_out);
endmodule
