// Logisim project latch_D_sincrono.circ as structural Verilog: 4 circuits, main circuit Latch D sync
module Latch_SR (
  input  Reset,
  input  Set,
  output Q,
  output nQ
);

  nor nor_1 (Q, Reset, nQ);
  nor nor_2 (nQ, Q, Set);
endmodule

module Latch_SR_sync (
  input  Reset,
  input  Clock,
  input  Set,
  output Q,
  output nQ
);

  wire and_1_out, and_2_out;

  and and_1 (and_1_out, Reset, Clock);
  and and_2 (and_2_out, Clock, Set);
  Latch_SR latch_sr_1 (.Reset(and_1_out), .Set(and_2_out), .Q(Q), .nQ(nQ));
endmodule

module Latch_D_sync (
  input  D,
  input  Clock,
  output Q,
  output nQ
);

  wire not_1_out;

  not not_1 (not_1_out, D);
  Latch_SR_sync latch_sr_sync_1 (.Reset(not_1_out), .Clock(Clock), .Set(D), .Q(Q), .nQ(nQ));
endmodule

module main (
  output Q,
  output nQ
);

  wire button_1_out, clock_1_out;

  Button button_1 (.out(button_1_out));
  Clock clock_1 (.out(clock_1_out));
  Latch_D_sync latch_d_sync_1 (.D(button_1_out), .Clock(clock_1_out), .Q(Q), .nQ(nQ));
endmodule
