// Logisim project scorrimento.circ as structural Verilog: 5 circuits, main circuit Es 6
module Latch_SC (
  input  Clear,
  input  Set,
  output Q,
  output nQ
);

  nor nor_1 (Q, Clear, nQ);
  nor nor_2 (nQ, Q, Set);
endmodule

module Latch_SC_sync (
  input  Clear,
  input  Clock,
  input  Set,
  output Q,
  output nQ
);

  wire and_1_out, and_2_out;

  and and_1 (and_1_out, Clear, Clock);
  and and_2 (and_2_out, Clock, Set);
  Latch_SC latch_sc_1 (.Clear(and_1_out), .Set(and_2_out), .Q(Q), .nQ(nQ));
endmodule

module Latch_D_sync (
  input  D,
  input  Clock,
  output Q,
  output out_4
);

  wire not_1_out;

  not not_1 (not_1_out, D);
  Latch_SC_sync latch_sc_sync_1 (.Clear(not_1_out), .Clock(Clock), .Set(D), .Q(Q), .nQ(out_4));
endmodule

module Flip_flop (
  input  D,
  input  Clock,
  output out_3
);

  wire latch_d_sync_1_q, not_1_out;

  Latch_D_sync latch_d_sync_1 (.D(D), .Clock(Clock), .Q(latch_d_sync_1_q));  // open: out_4
  not not_1 (not_1_out, Clock);
  Latch_D_sync latch_d_sync_2 (.D(latch_d_sync_1_q), .Clock(not_1_out), .Q(out_3));  // open: out_4

  // Notes on the sheet:
  //   Latch D
  //   Latch D
endmodule

module Es_6 (
  input  in,
  input  Clock,
  output [3:0] out_3,
  output [3:0] out_4,
  output [3:0] out_5
);

  wire not_1_out, not_2_out, not_3_out;

  Latch_D_sync latch_d_sync_1 (.D(in), .Clock(Clock), .Q(out_3[0]));  // open: out_4
  Latch_D_sync latch_d_sync_2 (.D(in), .Clock(Clock), .Q(out_4[0]));  // open: out_4
  not not_1 (not_1_out, Clock);
  Flip_flop flip_flop_1 (.D(in), .Clock(Clock), .out_3(out_5[0]));
  Latch_D_sync latch_d_sync_3 (.D(out_3[1]), .Clock(Clock), .Q(out_3[2]));  // open: out_4
  Latch_D_sync latch_d_sync_4 (.D(out_3[0]), .Clock(Clock), .Q(out_3[1]));  // open: out_4
  Latch_D_sync latch_d_sync_5 (.D(out_4[0]), .Clock(not_1_out), .Q(out_4[1]));  // open: out_4
  Latch_D_sync latch_d_sync_6 (.D(out_4[1]), .Clock(not_2_out), .Q(out_4[2]));  // open: out_4
  not not_2 (not_2_out, not_1_out);
  Flip_flop flip_flop_2 (.D(out_5[1]), .Clock(Clock), .out_3(out_5[2]));
  Flip_flop flip_flop_3 (.D(out_5[0]), .Clock(Clock), .out_3(out_5[1]));
  Latch_D_sync latch_d_sync_7 (.D(out_3[2]), .Clock(Clock), .Q(out_3[3]));  // open: out_4
  Latch_D_sync latch_d_sync_8 (.D(out_4[2]), .Clock(not_3_out), .Q(out_4[3]));  // open: out_4
  not not_3 (not_3_out, not_2_out);
  Flip_flop flip_flop_4 (.D(out_5[2]), .Clock(Clock), .out_3(out_5[3]));

  // Notes on the sheet:
  //   Uso di Latch D
  //   Uso di Latch D con inverter
  //   Uso di Flip-flop
endmodule
