// Logisim project memoria_shift.circ as structural Verilog: 5 circuits, main circuit Es 7
module Es_7 (
  input  [3:0] in_1,
  input  Clock,
  input  Reset,
  input  Write,
  input  Shift,
  input  shift_in,
  output [3:0] out_7
);

  wire and_2_out, multiplexer_1_out, multiplexer_2_out, multiplexer_3_out, multiplexer_4_out, not_2_out,
       or_1_out;
  wire [3:0] and_1_out;
  wire [3:3] not_1_out;

  not not_1 (not_1_out[3], Reset);
  or or_1 (or_1_out, Reset, Write, Shift);
  assign and_1_out = in_1 & {4{not_1_out[3]}};  // AND_Gate and_1, 4 bits wide
  and and_2 (and_2_out, Clock, or_1_out);
  not not_2 (not_2_out, Shift);
  Multiplexer #(.enable("false")) multiplexer_1 (
    .in0(shift_in), .in1(and_1_out[3]), .out(multiplexer_1_out), .sel(not_2_out));
  Flip_flop flip_flop_1 (.D(multiplexer_1_out), .Clock(and_2_out), .out_3(out_7[3]));
  Multiplexer #(.enable("false")) multiplexer_2 (
    .in0(out_7[3]), .in1(and_1_out[2]), .out(multiplexer_2_out), .sel(not_2_out));
  Multiplexer #(.enable("false")) multiplexer_3 (
    .in0(out_7[2]), .in1(and_1_out[1]), .out(multiplexer_3_out), .sel(not_2_out));
  Flip_flop flip_flop_2 (.D(multiplexer_2_out), .Clock(and_2_out), .out_3(out_7[2]));
  Multiplexer #(.enable("false")) multiplexer_4 (
    .in0(out_7[1]), .in1(and_1_out[0]), .out(multiplexer_4_out), .sel(not_2_out));
  Flip_flop flip_flop_3 (.D(multiplexer_3_out), .Clock(and_2_out), .out_3(out_7[1]));
  Flip_flop flip_flop_4 (.D(multiplexer_4_out), .Clock(and_2_out), .out_3(out_7[0]));
endmodule

module Latch_SC (
  input  Clear,
  input  Set,
  output Q,
  output nQ
);

  nor nor_1 (Q, Clear, nQ);
  nor nor_2 (nQ, Q, Set);
endmodule

module Latch_SC_sync (
  input  Clear,
  input  Clock,
  input  Set,
  output Q,
  output nQ
);

  wire and_1_out, and_2_out;

  and and_1 (and_1_out, Clear, Clock);
  and and_2 (and_2_out, Clock, Set);
  Latch_SC latch_sc_1 (.Clear(and_1_out), .Set(and_2_out), .Q(Q), .nQ(nQ));
endmodule

module Latch_D_sync (
  input  D,
  input  Clock,
  output Q,
  output out_4
);

  wire not_1_out;

  not not_1 (not_1_out, D);
  Latch_SC_sync latch_sc_sync_1 (.Clear(not_1_out), .Clock(Clock), .Set(D), .Q(Q), .nQ(out_4));
endmodule

module Flip_flop (
  input  D,
  input  Clock,
  output out_3
);

  wire latch_d_sync_1_q, not_1_out;

  Latch_D_sync latch_d_sync_1 (.D(D), .Clock(Clock), .Q(latch_d_sync_1_q));  // open: out_4
  not not_1 (not_1_out, Clock);
  Latch_D_sync latch_d_sync_2 (.D(latch_d_sync_1_q), .Clock(not_1_out), .Q(out_3));  // open: out_4

  // Notes on the sheet:
  //   Latch D
  //   Latch D
endmodule
