// Logisim project sommabinaria.circ as structural Verilog: 4 circuits, main circuit sommatoreMSF
module \output  (
  input  S,
  output \output 
);


  assign \output  = S;
endmodule

module Next (
  input  A,
  input  B,
  input  S,
  input  R,
  output S_prime,
  output R_prime
);

  wire and_1_out, and_2_out, xor_1_out;

  xor xor_1 (xor_1_out, B, A);
  xor xor_2 (S_prime, R, xor_1_out);
  and and_1 (and_1_out, R, xor_1_out);
  and and_2 (and_2_out, B, A);
  or or_1 (R_prime, and_1_out, and_2_out);
  // also tied to GND on the sheet: S
endmodule

module sommatoreMSF (
  input  A,
  input  B,
  input  clock,
  output \output 
);

  wire d_ff_1_q, d_ff_2_q, next_1_r_prime, next_1_s_prime;

  Next next_1 (.S_prime(next_1_s_prime), .R_prime(next_1_r_prime), .A(A), .B(B), .R(d_ff_2_q));  // open: S
  D_Flip_Flop d_ff_1 (.clk(clock), .D(next_1_s_prime), .Q(d_ff_1_q));  // open: Qn, preset, en, reset
  D_Flip_Flop d_ff_2 (.clk(clock), .D(next_1_r_prime), .Q(d_ff_2_q));  // open: Qn, preset, en, reset
  \output  output_1 (.S(d_ff_1_q), .\output (\output ));
endmodule

module sommatore4bit (
  input  [3:0] A,
  input  [3:0] B,
  output [3:0] out_3
);

  wire and_1_out, clock_1_out, counter_1_carry, multiplexer_1_out, multiplexer_2_out, not_1_out, write_out;
  wire [2:0] counter_1_q;

  not not_1 (not_1_out, counter_1_carry);
  Clock clock_1 (.out(clock_1_out));
  Button write (.out(write_out));
  Counter #(.width(3), .max('h4)) counter_1 (
    .Q(counter_1_q), .carry(counter_1_carry), .clk(and_1_out), .clr(write_out));  // open: load, D, count
  and and_1 (and_1_out, not_1_out, clock_1_out);
  Multiplexer #(.select(3), .enable("false")) multiplexer_1 (
    .in0(A[0]), .in1(A[1]), .in2(A[2]), .in3(A[3]), .out(multiplexer_1_out), .sel(counter_1_q));  // open: in4, in5, in6, in7
  Multiplexer #(.select(3), .enable("false")) multiplexer_2 (
    .in0(B[0]), .in1(B[1]), .in2(B[2]), .in3(B[3]), .out(multiplexer_2_out), .sel(counter_1_q));  // open: in4, in5, in6, in7
  sommatoreMSF sommatoremsf_1 (.A(multiplexer_1_out), .B(multiplexer_2_out), .\output (out_3[3]), .clock(and_1_out));
  D_Flip_Flop d_ff_1 (.clk(and_1_out), .D(out_3[3]), .Q(out_3[2]));  // open: Qn, preset, en, reset
  D_Flip_Flop d_ff_2 (.clk(and_1_out), .D(out_3[2]), .Q(out_3[1]));  // open: Qn, preset, en, reset
  D_Flip_Flop d_ff_3 (.clk(and_1_out), .D(out_3[1]), .Q(out_3[0]));  // open: Qn, preset, en, reset

  // Notes on the sheet:
  //   SommatoreMSF
endmodule
